# Fritzing sketch coffee-machine (saved by Fritzing 0.9.3b)
breadboards: 1

parts:
  R1 = Resistor [tolerance=±5% resistance=15 package=THT]
  R2 = Resistor [tolerance=±5% resistance=120 package="2512 [SMD]"]
  R2_2 = Resistor [tolerance=±5% resistance=120 package="2010 [SMD]"]
  R2_3 = Resistor [tolerance=±5% resistance=12k package="1206 [SMD]"]
  D1 = Rectifier Diode [part_number=1N4001 package="300 mil [THT]"]
  D2 = Rectifier Diode [part_number=1N4001 package="300 mil [THT]"]
  R3 = Resistor [tolerance=±5% resistance=1.2M package=THT]
  IC1 = IC, DIP package, 16 pins [chip_label=4017]
  IC2 = IC, DIP package, 16 pins [chip_label=4017]
  D3 = Zener Diode [part_number=1N4732A breakdown_voltage=3.6V package="300 mil [THT]"]
  C1 = Electrolytic Capacitor [capacitance=1000µF package="300 mil [THT, electrolytic]"]
  U1 = TRIAC [package=sot223]
  D4 = Diode [package=diode-hv]
  D5 = Diode [package=diode-hv]
  R3_2 = Resistor [tolerance=±5% resistance=1k package=THT]
  R4 = Resistor [tolerance=±5% resistance=3.3k package=THT]
  R5 = Resistor [tolerance=±5% resistance=10k package=THT]
  DIN1 = DIN-5 jack (MIDI) [package=THT]  # not connected

nets:
  N1: R1.Pin_0, IC2.pin16, D3.anode, C1.+, R5.Pin_1
  N2: R1.Pin_1, R2.Pin_0, R2_2.Pin_0, R2_3.Pin_0
  N3: R2.Pin_1, R2_2.Pin_1, R2_3.Pin_1, D1.anode
  N4: D1.cathode, D2.cathode
  N5: D2.anode, R3.Pin_0
  N6: R3.Pin_1, IC1.pin14
  N7: IC1.pin1, IC1.pin15
  N8: IC1.pin8, IC1.pin13, IC2.pin8, D3.cathode, C1.-, R4.Pin_0
  N9: IC1.pin10, IC2.pin14
  N10: IC2.pin5, D5.C, R3_2.Pin_1
  N11: IC2.pin15, D4.C, R5.Pin_0
  N12: U1.G, R3_2.Pin_0, R4.Pin_1
